# Fritzing sketch led_strip_breadboard (saved by Fritzing 0.9.3b)
breadboards: 1

parts:
  Q1 = MOSFET-NCHANNEL [package=to220v]
  ENCODER1 = Rotary Encoder with Knob
  J1 = male pin header, 4 pins [form="♂ (male)"]
  R1 = Resistor [tolerance=±5% resistance=220 package=THT]
  J2 = Camdenboss CTB0158-2 [part_number=CTB0158-2 package=THT]
  WeMos_D1_Mini1 = WeMos D1 Mini

nets:
  N1: Q1.G, R1.Pin_1
  N2: Q1.D, J2.pin1
  GND: Q1.S, ENCODER1.no_name_yet#2, ENCODER1.no_name_yet#5, J1.pin2, WeMos_D1_Mini1.G
  N3: ENCODER1.no_name_yet#1, WeMos_D1_Mini1.D5
  N4: ENCODER1.no_name_yet#3, WeMos_D1_Mini1.D6
  N5: ENCODER1.no_name_yet#4, WeMos_D1_Mini1.D4
  5V: J1.pin1, WeMos_D1_Mini1.5V
  12V: J1.pin3, J2.pin2
  N6: R1.Pin_0, WeMos_D1_Mini1.D2

notes:
  12V
  5V
  Random four pins is a Pololu 5V regulator that I had 'lying around'. But any 12 to 5V reg will work.

custom parts:
  Rotary Encoder with Knob: Rotary Encoder with 1/4" Shaft and Knob
